# Fritzing sketch SmartGarden2 (saved by Fritzing 0.9.3b)

parts:
  U1 = NodeMCU V1.0
  Componente1 = Soil Moisture Sensor
  Rele1 = Keyes Relay [package=THT]
  M1 = DC Motor

nets:
  3V3: U1.3V3, Componente1.VCC, Rele1.signal, Rele1.C
  GND: U1.GND, Componente1.GND, Rele1.ground, M1.pin_1
  N1: U1.D6, Rele1.power
  N2: U1.A0, Componente1.SIG
  N3: Rele1.NO, M1.pin_2

custom parts:
  NodeMCU V1.0: ESP8266 based NodeMCU
  Keyes Relay: The Keyes 5V relay module is suitable for SCM development, home appliance control. It uses a 5V~12V TIL control signal which can control DC / AC signal.
